# Fritzing sketch multi (saved by Fritzing 0.8.7b)
breadboards: 1

parts:
  LED7 = RGB LED (com. anode, rbg) [package="5 mm [THT]"]
  R1 = PHOTOCELL [package=photocell-kit]
  Part1 = Arduino Uno (Rev3)
  R2 = Resistor [tolerance=±5% resistance=220 package=THT]
  R3 = Resistor [tolerance=±5% resistance=220 package=THT]
  R4 = Resistor [tolerance=±5% resistance=220 package=THT]

nets:
  N1: LED7.red_cathode, R2.Pin_0
  N2: LED7.common_anode, R1.P$1, Part1.GND
  N3: LED7.blue_cathode, R3.Pin_0
  N4: LED7.green_cathode, R4.Pin_0
  N5: R1.P$2, Part1.5V
  N6: Part1.D11_PWM/MOSI, R4.Pin_1
  N7: Part1.D12/MISO, R3.Pin_1
  N8: Part1.D13/SCK, R2.Pin_1
